// Logisim project AR8.circ as structural Verilog: 61 circuits, main circuit AR8PROCESSOR
module MUX3_8Bits (
  input  [2:0] slct,
  input  [7:0] S1,
  input  [7:0] S2,
  input  [7:0] S3,
  input  [7:0] S4,
  input  [7:0] S5,
  input  [7:0] S6,
  input  [7:0] S7,
  input  [7:0] S8,
  output [7:0] S
);

  wire not_1_out, not_2_out, not_3_out, not_4_out, not_5_out, not_6_out, not_7_out, not_8_out, not_9_out,
       not_10_out, not_11_out, not_12_out;
  wire [7:0] and_9_out, and_10_out, and_11_out, and_12_out, and_13_out, and_14_out, and_15_out, and_16_out;
  wire [7:7] and_1_out, and_2_out, and_3_out, and_4_out, and_5_out, and_6_out, and_7_out, and_8_out;

  not not_1 (not_1_out, slct[0]);
  not not_2 (not_2_out, slct[1]);
  not not_3 (not_3_out, slct[2]);
  not not_4 (not_4_out, slct[1]);
  not not_5 (not_5_out, slct[2]);
  not not_6 (not_6_out, slct[0]);
  not not_7 (not_7_out, slct[2]);
  not not_8 (not_8_out, slct[2]);
  not not_9 (not_9_out, slct[0]);
  not not_10 (not_10_out, slct[1]);
  not not_11 (not_11_out, slct[1]);
  not not_12 (not_12_out, slct[0]);
  and and_1 (and_1_out[7], not_1_out, not_2_out, not_3_out);
  and and_2 (and_2_out[7], slct[0], not_4_out, not_5_out);
  and and_3 (and_3_out[7], not_6_out, slct[1], not_7_out);
  and and_4 (and_4_out[7], slct[0], slct[1], not_8_out);
  and and_5 (and_5_out[7], not_9_out, not_10_out, slct[2]);
  and and_6 (and_6_out[7], slct[0], not_11_out, slct[2]);
  and and_7 (and_7_out[7], not_12_out, slct[1], slct[2]);
  and and_8 (and_8_out[7], slct[0], slct[1], slct[2]);
  assign and_9_out = {8{and_1_out[7]}} & S1;  // AND_Gate and_9, 8 bits wide
  assign and_10_out = {8{and_2_out[7]}} & S2;  // AND_Gate and_10, 8 bits wide
  assign and_11_out = {8{and_3_out[7]}} & S3;  // AND_Gate and_11, 8 bits wide
  assign and_12_out = {8{and_4_out[7]}} & S4;  // AND_Gate and_12, 8 bits wide
  assign and_13_out = {8{and_5_out[7]}} & S5;  // AND_Gate and_13, 8 bits wide
  assign and_14_out = {8{and_6_out[7]}} & S6;  // AND_Gate and_14, 8 bits wide
  assign and_15_out = {8{and_7_out[7]}} & S7;  // AND_Gate and_15, 8 bits wide
  assign and_16_out = {8{and_8_out[7]}} & S8;  // AND_Gate and_16, 8 bits wide
  assign S = and_9_out | and_10_out | and_11_out | and_12_out | and_13_out | and_14_out | and_15_out | and_16_out;  // OR_Gate or_1, 8 bits wide
endmodule

module MUX2_8Bits (
  input  [7:0] S1,
  input  [7:0] S2,
  input  [7:0] S3,
  input  [7:0] S4,
  input  [1:0] slct,
  output [7:0] S
);

  MUX3_8Bits mux3_8bits_1 (.S1(S1), .S2(S2), .S3(S3), .S4(S4), .slct({1'b0, slct}), .S(S));  // open: S8, S5, S6, S7
endmodule

module MUX1_8Bits (
  input  [7:0] S1,
  input  [7:0] S2,
  input  slct,
  output [7:0] S
);

  MUX2_8Bits mux2_8bits_1 (.S1(S1), .S2(S2), .slct({1'b0, slct}), .S(S));  // open: S3, S4
endmodule

module MUX3_1Bit (
  input  S1,
  input  S2,
  input  S3,
  input  S4,
  input  S5,
  input  S6,
  input  S7,
  input  S8,
  input  [2:0] slct,
  output S
);

  wire [7:1] mux3_8bits_1_s;

  MUX3_8Bits mux3_8bits_1 (
    .S8({{7{1'b0}}, S8}), .S1({{7{1'b0}}, S1}), .S2({{7{1'b0}}, S2}), .S3({{7{1'b0}}, S3}),
    .S4({{7{1'b0}}, S4}), .S5({{7{1'b0}}, S5}), .S6({{7{1'b0}}, S6}), .S7({{7{1'b0}}, S7}), .slct(slct),
    .S({mux3_8bits_1_s, S}));
endmodule

module MUX2_1Bit (
  input  S1,
  input  S2,
  input  S3,
  input  S4,
  input  [1:0] slct,
  output S
);

  MUX3_1Bit mux3_1bit_1 (.S1(S1), .S2(S2), .S3(S3), .S4(S4), .slct({1'b0, slct}), .S(S));  // open: S5, S6, S7, S8
endmodule

module MUX1_1Bit (
  input  S1,
  input  S2,
  input  slct,
  output S
);

  MUX2_1Bit mux2_1bit_1 (.S1(S1), .S2(S2), .slct({1'b0, slct}), .S(S));  // open: S3, S4
endmodule

module MUX1_3Bits (
  input  [2:0] S1,
  input  [2:0] S2,
  input  slct,
  output [2:0] S
);

  MUX1_1Bit mux1_1bit_1 (.S1(S1[0]), .S2(S2[0]), .slct(slct), .S(S[0]));
  MUX1_1Bit mux1_1bit_2 (.S1(S1[1]), .S2(S2[1]), .slct(slct), .S(S[1]));
  MUX1_1Bit mux1_1bit_3 (.S1(S1[2]), .S2(S2[2]), .slct(slct), .S(S[2]));
endmodule

module DEC3_1Bit (
  input  WE,
  input  [2:0] slct,
  output WE1,
  output WE2,
  output WE3,
  output WE4,
  output WE5,
  output WE6,
  output WE7,
  output WE8
);

  wire not_1_out, not_2_out, not_3_out, not_4_out, not_5_out, not_6_out, not_7_out, not_8_out, not_9_out,
       not_10_out, not_11_out, not_12_out;

  not not_1 (not_1_out, slct[0]);
  not not_2 (not_2_out, slct[1]);
  not not_3 (not_3_out, slct[1]);
  not not_4 (not_4_out, slct[0]);
  not not_5 (not_5_out, slct[0]);
  not not_6 (not_6_out, slct[1]);
  not not_7 (not_7_out, slct[1]);
  not not_8 (not_8_out, slct[0]);
  not not_9 (not_9_out, slct[2]);
  not not_10 (not_10_out, slct[2]);
  not not_11 (not_11_out, slct[2]);
  not not_12 (not_12_out, slct[2]);
  and and_1 (WE1, not_1_out, not_2_out, not_9_out, WE);
  and and_2 (WE2, slct[0], not_3_out, not_10_out, WE);
  and and_3 (WE3, not_4_out, slct[1], not_11_out, WE);
  and and_4 (WE4, slct[0], slct[1], not_12_out, WE);
  and and_5 (WE5, not_5_out, not_6_out, slct[2], WE);
  and and_6 (WE6, slct[0], not_7_out, slct[2], WE);
  and and_7 (WE7, not_8_out, slct[1], slct[2], WE);
  and and_8 (WE8, slct[0], slct[1], slct[2], WE);
endmodule

module ADD1Bit (
  input  a,
  input  b,
  output s,
  output r
);

  xor xor_1 (s, a, b);
  and and_1 (r, a, b);

  // Notes on the sheet:
  //   a: initial=0x1
endmodule

module ADD1BitComplete (
  input  c,
  input  a,
  input  b,
  output s,
  output r
);

  wire add1bit_1_r, add1bit_1_s, add1bit_2_r;

  ADD1Bit add1bit_1 (.a(a), .b(b), .s(add1bit_1_s), .r(add1bit_1_r));
  ADD1Bit add1bit_2 (.a(add1bit_1_s), .b(c), .s(s), .r(add1bit_2_r));
  or or_1 (r, add1bit_2_r, add1bit_1_r);

  // Notes on the sheet:
  //   a: initial=0x1
endmodule

module ADD8Bits (
  input  [7:0] A,
  input  [7:0] B,
  output [7:0] S,
  output O
);

  wire add1bit_1_r, add1bitcomplete_1_r, add1bitcomplete_2_r, add1bitcomplete_3_r, add1bitcomplete_4_r,
       add1bitcomplete_5_r, add1bitcomplete_6_r;

  ADD1Bit add1bit_1 (.a(A[0]), .b(B[0]), .s(S[0]), .r(add1bit_1_r));
  ADD1BitComplete add1bitcomplete_1 (.c(add1bit_1_r), .a(A[1]), .b(B[1]), .s(S[1]), .r(add1bitcomplete_1_r));
  ADD1BitComplete add1bitcomplete_2 (.c(add1bitcomplete_1_r), .a(A[2]), .b(B[2]), .s(S[2]), .r(add1bitcomplete_2_r));
  ADD1BitComplete add1bitcomplete_3 (.c(add1bitcomplete_2_r), .a(A[3]), .b(B[3]), .s(S[3]), .r(add1bitcomplete_3_r));
  ADD1BitComplete add1bitcomplete_4 (.c(add1bitcomplete_3_r), .a(A[4]), .b(B[4]), .s(S[4]), .r(add1bitcomplete_4_r));
  ADD1BitComplete add1bitcomplete_5 (.c(add1bitcomplete_4_r), .a(A[5]), .b(B[5]), .s(S[5]), .r(add1bitcomplete_5_r));
  ADD1BitComplete add1bitcomplete_6 (.c(add1bitcomplete_5_r), .a(A[6]), .b(B[6]), .s(S[6]), .r(add1bitcomplete_6_r));
  ADD1BitComplete add1bitcomplete_7 (.c(add1bitcomplete_6_r), .a(A[7]), .b(B[7]), .s(S[7]), .r(O));
endmodule

module COMPLEMENT8BIts (
  input  [7:0] A,
  output [7:0] S
);

  wire [7:0] not_1_out;

  assign not_1_out = ~A;  // NOT_Gate not_1, 8 bits wide
  ADD8Bits add8bits_1 (.A(not_1_out), .B(8'h1), .S(S));  // open: O
endmodule

module SUB8Bits (
  input  [7:0] A,
  input  [7:0] B,
  output [7:0] S
);

  wire [7:0] complement8bits_1_s;

  COMPLEMENT8BIts complement8bits_1 (.A(B), .S(complement8bits_1_s));
  ADD8Bits add8bits_1 (.A(A), .B(complement8bits_1_s), .S(S));  // open: O
endmodule

module MIN8Bits (
  input  [7:0] A,
  input  [7:0] B,
  output [7:0] S
);

  wire cmp_gt8bits_1_s;

  CMP_GT8Bits cmp_gt8bits_1 (.A(A), .B(B), .S(cmp_gt8bits_1_s));
  MUX1_8Bits mux1_8bits_1 (.S1(A), .S2(B), .slct(cmp_gt8bits_1_s), .S(S));
endmodule

module MAX8Bits (
  input  [7:0] A,
  input  [7:0] B,
  output [7:0] S
);

  wire cmp_lt8bits_1_i;

  CMP_LT8Bits cmp_lt8bits_1 (.A(A), .B(B), .I(cmp_lt8bits_1_i));
  MUX1_8Bits mux1_8bits_1 (.S1(A), .S2(B), .slct(cmp_lt8bits_1_i), .S(S));
endmodule

module Arithmetic2Block (
  input  [7:0] A,
  input  [7:0] B,
  input  [2:0] OP,
  output [7:0] S,
  output E
);

  wire add8bits_1_o;
  wire [7:0] add8bits_1_s, max8bits_1_s, min8bits_1_s, sub8bits_1_s;

  ADD8Bits add8bits_1 (.A(A), .B(B), .S(add8bits_1_s), .O(add8bits_1_o));
  SUB8Bits sub8bits_1 (.A(A), .B(B), .S(sub8bits_1_s));
  MIN8Bits min8bits_1 (.A(A), .B(B), .S(min8bits_1_s));
  MAX8Bits max8bits_1 (.A(A), .B(B), .S(max8bits_1_s));
  MUX3_8Bits mux3_8bits_1 (
    .S1(add8bits_1_s), .S2(sub8bits_1_s), .S3(min8bits_1_s), .S4(max8bits_1_s), .slct(OP), .S(S));  // open: S8, S5, S6, S7
  MUX3_1Bit mux3_1bit_1 (
    .S1(add8bits_1_o), .S2(1'b0), .S3(1'b0), .S4(1'b0), .S5(1'b1), .S6(1'b1), .S7(1'b1), .S8(1'b1),
    .slct(OP), .S(E));
endmodule

module INC8Bits (
  input  [7:0] A,
  output [7:0] S,
  output O
);

  ADD8Bits add8bits_1 (.A(A), .B(8'h1), .S(S), .O(O));
endmodule

module DEC8Bits (
  input  [7:0] A,
  output [7:0] S
);

  SUB8Bits sub8bits_1 (.A(A), .B(8'h1), .S(S));
endmodule

module NEG8Bits (
  input  [7:0] A,
  output [7:0] S
);

  SUB8Bits sub8bits_1 (.A({8{1'b0}}), .B(A), .S(S));
endmodule

module ABS8Bits (
  input  [7:0] A,
  output [7:0] S
);

  wire [7:0] neg8bits_1_s;

  NEG8Bits neg8bits_1 (.A(A), .S(neg8bits_1_s));
  MUX1_8Bits mux1_8bits_1 (.S1(A), .S2(neg8bits_1_s), .slct(A[7]), .S(S));
endmodule

module Arithmetic1Block (
  input  [7:0] A,
  input  [2:0] OP,
  output [7:0] S,
  output E
);

  wire inc8bits_1_o;
  wire [7:0] abs8bits_1_s, dec8bits_1_s, inc8bits_1_s, neg8bits_1_s;

  INC8Bits inc8bits_1 (.A(A), .S(inc8bits_1_s), .O(inc8bits_1_o));
  DEC8Bits dec8bits_1 (.A(A), .S(dec8bits_1_s));
  NEG8Bits neg8bits_1 (.A(A), .S(neg8bits_1_s));
  ABS8Bits abs8bits_1 (.A(A), .S(abs8bits_1_s));
  MUX3_8Bits mux3_8bits_1 (
    .S8(abs8bits_1_s), .S5(inc8bits_1_s), .S6(dec8bits_1_s), .S7(neg8bits_1_s), .slct(OP), .S(S));  // open: S1, S2, S3, S4
  MUX3_1Bit mux3_1bit_1 (
    .S1(inc8bits_1_o), .S2(1'b1), .S3(1'b1), .S4(1'b1), .S5(1'b0), .S6(1'b0), .S7(1'b0), .S8(1'b0),
    .slct(OP), .S(E));
endmodule

module AND8Bits (
  input  [7:0] A,
  input  [7:0] B,
  output [7:0] S
);

  assign S = A & B;  // AND_Gate and_1, 8 bits wide
endmodule

module OR8Bits (
  input  [7:0] A,
  input  [7:0] B,
  output [7:0] S
);

  assign S = A | B;  // OR_Gate or_1, 8 bits wide
endmodule

module XOR8Bits (
  input  [7:0] A,
  input  [7:0] B,
  output [7:0] S
);

  assign S = A ^ B;  // XOR_Gate xor_1, 8 bits wide
endmodule

module NAND8Bits (
  input  [7:0] A,
  input  [7:0] B,
  output [7:0] S
);

  wire [7:0] and8bits_1_s;

  AND8Bits and8bits_1 (.A(A), .B(B), .S(and8bits_1_s));
  NOT8Bits not8bits_1 (.A(and8bits_1_s), .S(S));
endmodule

module NOR8Bits (
  input  [7:0] A,
  input  [7:0] B,
  output [7:0] S
);

  wire [7:0] or8bits_1_s;

  OR8Bits or8bits_1 (.A(A), .B(B), .S(or8bits_1_s));
  NOT8Bits not8bits_1 (.A(or8bits_1_s), .S(S));
endmodule

module XNOR8Bits (
  input  [7:0] A,
  input  [7:0] B,
  output [7:0] S
);

  wire [7:0] xor8bits_1_s;

  XOR8Bits xor8bits_1 (.A(A), .B(B), .S(xor8bits_1_s));
  NOT8Bits not8bits_1 (.A(xor8bits_1_s), .S(S));
endmodule

module Logical2Block (
  input  [7:0] A,
  input  [7:0] B,
  input  [2:0] OP,
  output [7:0] S,
  output E
);

  wire [7:0] and8bits_1_s, nand8bits_1_s, nor8bits_1_s, or8bits_1_s, xnor8bits_1_s, xor8bits_1_s;

  AND8Bits and8bits_1 (.A(A), .B(B), .S(and8bits_1_s));
  OR8Bits or8bits_1 (.A(A), .B(B), .S(or8bits_1_s));
  XOR8Bits xor8bits_1 (.A(A), .B(B), .S(xor8bits_1_s));
  NAND8Bits nand8bits_1 (.A(A), .B(B), .S(nand8bits_1_s));
  NOR8Bits nor8bits_1 (.A(A), .B(B), .S(nor8bits_1_s));
  XNOR8Bits xnor8bits_1 (.A(A), .B(B), .S(xnor8bits_1_s));
  MUX3_8Bits mux3_8bits_1 (
    .S1(and8bits_1_s), .S2(or8bits_1_s), .S3(xor8bits_1_s), .S4(nand8bits_1_s), .S5(nor8bits_1_s),
    .S6(xnor8bits_1_s), .slct(OP), .S(S));  // open: S8, S7
  MUX3_1Bit mux3_1bit_1 (
    .S1(1'b0), .S2(1'b0), .S3(1'b0), .S4(1'b0), .S5(1'b0), .S6(1'b0), .S7(1'b1), .S8(1'b1), .slct(OP), .S(E));
endmodule

module NOT8Bits (
  input  [7:0] A,
  output [7:0] S
);

  assign S = ~A;  // NOT_Gate not_1, 8 bits wide
endmodule

module LSL3_8Bits (
  input  [7:0] A,
  input  [2:0] D,
  output [7:0] S
);

  MUX3_1Bit mux3_1bit_1 (
    .S1(A[0]), .S2(1'b0), .S3(1'b0), .S4(1'b0), .S5(1'b0), .S6(1'b0), .S7(1'b0), .S8(1'b0), .slct(D), .S(S[0]));
  MUX3_1Bit mux3_1bit_2 (
    .S1(A[1]), .S2(A[0]), .S3(1'b0), .S4(1'b0), .S5(1'b0), .S6(1'b0), .S7(1'b0), .S8(1'b0), .slct(D), .S(S[1]));
  MUX3_1Bit mux3_1bit_3 (
    .S1(A[2]), .S2(A[1]), .S3(A[0]), .S4(1'b0), .S5(1'b0), .S6(1'b0), .S7(1'b0), .S8(1'b0), .slct(D), .S(S[2]));
  MUX3_1Bit mux3_1bit_4 (
    .S1(A[3]), .S2(A[2]), .S3(A[1]), .S4(A[0]), .S5(1'b0), .S6(1'b0), .S7(1'b0), .S8(1'b0), .slct(D), .S(S[3]));
  MUX3_1Bit mux3_1bit_5 (
    .S1(A[4]), .S2(A[3]), .S3(A[2]), .S4(A[1]), .S5(A[0]), .S6(1'b0), .S7(1'b0), .S8(1'b0), .slct(D), .S(S[4]));
  MUX3_1Bit mux3_1bit_6 (
    .S1(A[5]), .S2(A[4]), .S3(A[3]), .S4(A[2]), .S5(A[1]), .S6(A[0]), .S7(1'b0), .S8(1'b0), .slct(D), .S(S[5]));
  MUX3_1Bit mux3_1bit_7 (
    .S1(A[6]), .S2(A[5]), .S3(A[4]), .S4(A[3]), .S5(A[2]), .S6(A[1]), .S7(A[0]), .S8(1'b0), .slct(D), .S(S[6]));
  MUX3_1Bit mux3_1bit_8 (
    .S1(A[7]), .S2(A[6]), .S3(A[5]), .S4(A[4]), .S5(A[3]), .S6(A[2]), .S7(A[1]), .S8(A[0]), .slct(D), .S(S[7]));
endmodule

module LSL8Bits (
  input  [7:0] A,
  output [7:0] S
);

  LSL3_8Bits lsl3_8bits_1 (.A(A), .D(3'b001), .S(S));
endmodule

module INVERTER8Bits (
  input  [7:0] A,
  output [7:0] S
);


  assign S = {A[0], A[1], A[2], A[3], A[4], A[5], A[6], A[7]};
endmodule

module LSR3_8Bits (
  input  [7:0] A,
  input  [2:0] D,
  output [7:0] S
);

  wire [7:0] inverter8bits_1_s, lsl3_8bits_1_s;

  INVERTER8Bits inverter8bits_1 (.A(A), .S(inverter8bits_1_s));
  LSL3_8Bits lsl3_8bits_1 (.A(inverter8bits_1_s), .D(D), .S(lsl3_8bits_1_s));
  INVERTER8Bits inverter8bits_2 (.A(lsl3_8bits_1_s), .S(S));
endmodule

module LSR8Bits (
  input  [7:0] A,
  output [7:0] S
);

  LSR3_8Bits lsr3_8bits_1 (.A(A), .D(3'b001), .S(S));
endmodule

module ASL8Bits (
  input  [7:0] A,
  output [7:0] S
);


  assign S = {A[7], A[5:0], 1'b0};
endmodule

module ASR8Bits (
  input  [7:0] A,
  output [7:0] S
);


  assign S = {{2{A[7]}}, A[6:1]};
endmodule

module ROL3_8Bits (
  input  [7:0] A,
  input  [2:0] D,
  output [7:0] S
);

  MUX3_1Bit mux3_1bit_1 (
    .S1(A[0]), .S2(A[7]), .S3(A[6]), .S4(A[5]), .S5(A[4]), .S6(A[3]), .S7(A[2]), .S8(A[1]), .slct(D), .S(S[0]));
  MUX3_1Bit mux3_1bit_2 (
    .S1(A[1]), .S2(A[0]), .S3(A[7]), .S4(A[6]), .S5(A[5]), .S6(A[4]), .S7(A[3]), .S8(A[2]), .slct(D), .S(S[1]));
  MUX3_1Bit mux3_1bit_3 (
    .S1(A[2]), .S2(A[1]), .S3(A[0]), .S4(A[7]), .S5(A[6]), .S6(A[5]), .S7(A[4]), .S8(A[3]), .slct(D), .S(S[2]));
  MUX3_1Bit mux3_1bit_4 (
    .S1(A[3]), .S2(A[2]), .S3(A[1]), .S4(A[0]), .S5(A[7]), .S6(A[6]), .S7(A[5]), .S8(A[4]), .slct(D), .S(S[3]));
  MUX3_1Bit mux3_1bit_5 (
    .S1(A[4]), .S2(A[3]), .S3(A[2]), .S4(A[1]), .S5(A[0]), .S6(A[7]), .S7(A[6]), .S8(A[5]), .slct(D), .S(S[4]));
  MUX3_1Bit mux3_1bit_6 (
    .S1(A[5]), .S2(A[4]), .S3(A[3]), .S4(A[2]), .S5(A[1]), .S6(A[0]), .S7(A[7]), .S8(A[6]), .slct(D), .S(S[5]));
  MUX3_1Bit mux3_1bit_7 (
    .S1(A[6]), .S2(A[5]), .S3(A[4]), .S4(A[3]), .S5(A[2]), .S6(A[1]), .S7(A[0]), .S8(A[7]), .slct(D), .S(S[6]));
  MUX3_1Bit mux3_1bit_8 (
    .S1(A[7]), .S2(A[6]), .S3(A[5]), .S4(A[4]), .S5(A[3]), .S6(A[2]), .S7(A[1]), .S8(A[0]), .slct(D), .S(S[7]));
endmodule

module ROL8Bits (
  input  [7:0] A,
  output [7:0] S
);

  ROL3_8Bits rol3_8bits_1 (.A(A), .D(3'b001), .S(S));
endmodule

module ROR3_8Bits (
  input  [7:0] A,
  input  [2:0] D,
  output [7:0] S
);

  wire [2:0] not_1_out;
  wire [7:0] rol3_8bits_1_s;

  assign not_1_out = ~D;  // NOT_Gate not_1, 3 bits wide
  ROL3_8Bits rol3_8bits_1 (.A(A), .D(not_1_out), .S(rol3_8bits_1_s));
  ROL3_8Bits rol3_8bits_2 (.A(rol3_8bits_1_s), .D(3'b001), .S(S));
endmodule

module ROR8Bits (
  input  [7:0] A,
  output [7:0] S
);

  ROR3_8Bits ror3_8bits_1 (.A(A), .D(3'b001), .S(S));
endmodule

module Logical1Block (
  input  [7:0] A,
  input  [2:0] OP,
  output [7:0] S,
  output E
);

  wire [7:0] asl8bits_1_s, asr8bits_1_s, lsl8bits_1_s, lsr8bits_1_s, not8bits_1_s, rol8bits_1_s, ror8bits_1_s;

  NOT8Bits not8bits_1 (.A(A), .S(not8bits_1_s));
  LSL8Bits lsl8bits_1 (.A(A), .S(lsl8bits_1_s));
  LSR8Bits lsr8bits_1 (.A(A), .S(lsr8bits_1_s));
  ASR8Bits asr8bits_1 (.A(A), .S(asr8bits_1_s));
  ROL8Bits rol8bits_1 (.A(A), .S(rol8bits_1_s));
  ROR8Bits ror8bits_1 (.A(A), .S(ror8bits_1_s));
  ASL8Bits asl8bits_1 (.A(A), .S(asl8bits_1_s));
  MUX3_8Bits mux3_8bits_1 (
    .S1(not8bits_1_s), .S2(lsl8bits_1_s), .S3(lsr8bits_1_s), .S4(asr8bits_1_s), .S5(rol8bits_1_s),
    .S6(ror8bits_1_s), .S7(asl8bits_1_s), .slct(OP), .S(S));  // open: S8
  MUX3_1Bit mux3_1bit_1 (
    .S1(1'b0), .S2(1'b0), .S3(1'b0), .S4(1'b0), .S5(1'b0), .S6(1'b0), .S7(1'b0), .S8(1'b1), .slct(OP), .S(E));
endmodule

module COMPARATOR1Bit (
  input  a,
  input  b,
  output i,
  output e,
  output s
);

  wire not_1_out, not_2_out, xor_1_out;

  not not_1 (not_1_out, a);
  xor xor_1 (xor_1_out, a, b);
  not not_2 (not_2_out, b);
  and and_1 (i, not_1_out, b);
  not not_3 (e, xor_1_out);
  and and_2 (s, a, not_2_out);

  // Notes on the sheet:
  //   a: initial=0x1
endmodule

module COMPARATOR1BitComplete (
  input  iin,
  input  ein,
  input  sin,
  input  a,
  input  b,
  output i,
  output e,
  output s
);

  wire and_1_out, and_2_out, comparator1bit_1_e, comparator1bit_1_i, comparator1bit_1_s;

  COMPARATOR1Bit comparator1bit_1 (
    .a(a), .b(b), .i(comparator1bit_1_i), .e(comparator1bit_1_e), .s(comparator1bit_1_s));
  and and_1 (and_1_out, comparator1bit_1_i, ein);
  and and_2 (and_2_out, comparator1bit_1_s, ein);
  or or_1 (i, iin, and_1_out);
  and and_3 (e, comparator1bit_1_e, ein);
  or or_2 (s, and_2_out, sin);

  // Notes on the sheet:
  //   a: initial=0x1
  //   iin: initial=0x1
endmodule

module COMPARATOR8Bits (
  input  [7:0] A,
  input  [7:0] B,
  output I,
  output E,
  output S
);

  wire comparator1bit_1_e, comparator1bit_1_i, comparator1bit_1_s, comparator1bitcomplete_2_e,
       comparator1bitcomplete_2_i, comparator1bitcomplete_2_s, comparator1bitcomplete_3_e,
       comparator1bitcomplete_3_i, comparator1bitcomplete_3_s, comparator1bitcomplete_4_e,
       comparator1bitcomplete_4_i, comparator1bitcomplete_4_s, comparator1bitcomplete_5_e,
       comparator1bitcomplete_5_i, comparator1bitcomplete_5_s, comparator1bitcomplete_6_e,
       comparator1bitcomplete_6_i, comparator1bitcomplete_6_s, comparator1bitcomplete_7_e,
       comparator1bitcomplete_7_i, comparator1bitcomplete_7_s;

  COMPARATOR1BitComplete comparator1bitcomplete_1 (
    .iin(comparator1bitcomplete_2_i), .ein(comparator1bitcomplete_2_e), .sin(comparator1bitcomplete_2_s),
    .a(A[0]), .b(B[0]), .i(I), .e(E), .s(S));
  COMPARATOR1BitComplete comparator1bitcomplete_2 (
    .iin(comparator1bitcomplete_3_i), .ein(comparator1bitcomplete_3_e), .sin(comparator1bitcomplete_3_s),
    .a(A[1]), .b(B[1]), .i(comparator1bitcomplete_2_i), .e(comparator1bitcomplete_2_e),
    .s(comparator1bitcomplete_2_s));
  COMPARATOR1BitComplete comparator1bitcomplete_3 (
    .iin(comparator1bitcomplete_4_i), .ein(comparator1bitcomplete_4_e), .sin(comparator1bitcomplete_4_s),
    .a(A[2]), .b(B[2]), .i(comparator1bitcomplete_3_i), .e(comparator1bitcomplete_3_e),
    .s(comparator1bitcomplete_3_s));
  COMPARATOR1BitComplete comparator1bitcomplete_4 (
    .iin(comparator1bitcomplete_5_i), .ein(comparator1bitcomplete_5_e), .sin(comparator1bitcomplete_5_s),
    .a(A[3]), .b(B[3]), .i(comparator1bitcomplete_4_i), .e(comparator1bitcomplete_4_e),
    .s(comparator1bitcomplete_4_s));
  COMPARATOR1BitComplete comparator1bitcomplete_5 (
    .iin(comparator1bitcomplete_6_i), .ein(comparator1bitcomplete_6_e), .sin(comparator1bitcomplete_6_s),
    .a(A[4]), .b(B[4]), .i(comparator1bitcomplete_5_i), .e(comparator1bitcomplete_5_e),
    .s(comparator1bitcomplete_5_s));
  COMPARATOR1BitComplete comparator1bitcomplete_6 (
    .iin(comparator1bitcomplete_7_i), .ein(comparator1bitcomplete_7_e), .sin(comparator1bitcomplete_7_s),
    .a(A[5]), .b(B[5]), .i(comparator1bitcomplete_6_i), .e(comparator1bitcomplete_6_e),
    .s(comparator1bitcomplete_6_s));
  COMPARATOR1BitComplete comparator1bitcomplete_7 (
    .iin(comparator1bit_1_i), .ein(comparator1bit_1_e), .sin(comparator1bit_1_s), .a(A[6]), .b(B[6]),
    .i(comparator1bitcomplete_7_i), .e(comparator1bitcomplete_7_e), .s(comparator1bitcomplete_7_s));
  COMPARATOR1Bit comparator1bit_1 (
    .a(A[7]), .b(B[7]), .i(comparator1bit_1_i), .e(comparator1bit_1_e), .s(comparator1bit_1_s));
endmodule

module CMP_LT8Bits (
  input  [7:0] A,
  input  [7:0] B,
  output I
);

  COMPARATOR8Bits comparator8bits_1 (.A(A), .B(B), .I(I));  // open: E, S
endmodule

module CMP_LE8Bits (
  input  [7:0] A,
  input  [7:0] B,
  output E
);

  wire cmp_gt8bits_1_s;

  CMP_GT8Bits cmp_gt8bits_1 (.A(A), .B(B), .S(cmp_gt8bits_1_s));
  not not_1 (E, cmp_gt8bits_1_s);
endmodule

module CMP_EQ8Bits (
  input  [7:0] A,
  input  [7:0] B,
  output E
);

  COMPARATOR8Bits comparator8bits_1 (.A(A), .B(B), .E(E));  // open: I, S
endmodule

module CMP_GE8Bits (
  input  [7:0] A,
  input  [7:0] B,
  output E
);

  wire cmp_lt8bits_1_i;

  CMP_LT8Bits cmp_lt8bits_1 (.A(A), .B(B), .I(cmp_lt8bits_1_i));
  not not_1 (E, cmp_lt8bits_1_i);
endmodule

module CMP_GT8Bits (
  input  [7:0] A,
  input  [7:0] B,
  output S
);

  COMPARATOR8Bits comparator8bits_1 (.A(A), .B(B), .S(S));  // open: I, E
endmodule

module CMP_NE8Bits (
  input  [7:0] A,
  input  [7:0] B,
  output D
);

  wire cmp_eq8bits_1_e;

  CMP_EQ8Bits cmp_eq8bits_1 (.A(A), .B(B), .E(cmp_eq8bits_1_e));
  not not_1 (D, cmp_eq8bits_1_e);
endmodule

module ComparisonBlock (
  input  [7:0] A,
  input  [7:0] B,
  input  [2:0] OP,
  output S,
  output E
);

  wire cmp_eq8bits_1_e, cmp_ge8bits_1_e, cmp_gt8bits_1_s, cmp_le8bits_1_e, cmp_lt8bits_1_i, cmp_ne8bits_1_d;

  CMP_LT8Bits cmp_lt8bits_1 (.A(A), .B(B), .I(cmp_lt8bits_1_i));
  CMP_LE8Bits cmp_le8bits_1 (.A(A), .B(B), .E(cmp_le8bits_1_e));
  CMP_EQ8Bits cmp_eq8bits_1 (.A(A), .B(B), .E(cmp_eq8bits_1_e));
  CMP_GE8Bits cmp_ge8bits_1 (.A(A), .B(B), .E(cmp_ge8bits_1_e));
  CMP_GT8Bits cmp_gt8bits_1 (.A(A), .B(B), .S(cmp_gt8bits_1_s));
  CMP_NE8Bits cmp_ne8bits_1 (.A(A), .B(B), .D(cmp_ne8bits_1_d));
  MUX3_1Bit mux3_1bit_1 (
    .S2(cmp_lt8bits_1_i), .S3(cmp_le8bits_1_e), .S4(cmp_eq8bits_1_e), .S5(cmp_ge8bits_1_e),
    .S6(cmp_gt8bits_1_s), .S7(cmp_ne8bits_1_d), .slct(OP), .S(S));  // open: S1, S8
  MUX3_1Bit mux3_1bit_2 (
    .S1(1'b1), .S2(1'b0), .S3(1'b0), .S4(1'b0), .S5(1'b0), .S6(1'b0), .S7(1'b0), .S8(1'b1), .slct(OP), .S(E));
endmodule

module ALU (
  input  [7:0] A,
  input  [7:0] B,
  input  [5:0] OP,
  output [7:0] S,
  output E
);

  wire arithmetic1block_1_e, arithmetic2block_1_e, comparisonblock_1_e, logical1block_1_e, logical2block_1_e;
  wire [0:0] comparisonblock_1_s;
  wire [7:0] arithmetic1block_1_s, arithmetic2block_1_s, logical1block_1_s, logical2block_1_s;

  Arithmetic2Block arithmetic2block_1 (.A(A), .B(B), .OP(OP[2:0]), .S(arithmetic2block_1_s), .E(arithmetic2block_1_e));
  Arithmetic1Block arithmetic1block_1 (.A(A), .OP(OP[2:0]), .S(arithmetic1block_1_s), .E(arithmetic1block_1_e));
  Logical2Block logical2block_1 (.A(A), .B(B), .OP(OP[2:0]), .S(logical2block_1_s), .E(logical2block_1_e));
  Logical1Block logical1block_1 (.A(A), .OP(OP[2:0]), .S(logical1block_1_s), .E(logical1block_1_e));
  ComparisonBlock comparisonblock_1 (.A(A), .B(B), .OP(OP[2:0]), .S(comparisonblock_1_s[0]), .E(comparisonblock_1_e));
  MUX3_8Bits mux3_8bits_1 (
    .S8({{7{1'b0}}, comparisonblock_1_s[0]}), .S1(arithmetic2block_1_s), .S2(arithmetic1block_1_s),
    .S3(logical2block_1_s), .S4(logical2block_1_s), .S5(logical1block_1_s), .S6(logical1block_1_s),
    .S7({{7{1'b0}}, comparisonblock_1_s[0]}), .slct(OP[5:3]), .S(S));
  MUX3_1Bit mux3_1bit_1 (
    .S1(arithmetic2block_1_e), .S2(arithmetic1block_1_e), .S3(logical2block_1_e), .S4(logical2block_1_e),
    .S5(logical1block_1_e), .S6(logical1block_1_e), .S7(comparisonblock_1_e), .S8(comparisonblock_1_e),
    .slct(OP[5:3]), .S(E));
endmodule

module REGISTER1Bit (
  input  C,
  input  WE,
  input  CLK,
  output S
);

  wire mux1_1bit_1_s;

  MUX1_1Bit mux1_1bit_1 (.S1(S), .S2(C), .slct(WE), .S(mux1_1bit_1_s));
  D_Flip_Flop d_ff_1 (.D(mux1_1bit_1_s), .clk(CLK), .Q(S));  // open: Qn, preset, reset
endmodule

module REGISTER8Bits (
  input  [7:0] C,
  input  WE,
  input  CLK,
  output [7:0] S
);

  REGISTER1Bit register1bit_1 (.C(C[0]), .WE(WE), .CLK(CLK), .S(S[0]));
  REGISTER1Bit register1bit_2 (.C(C[1]), .WE(WE), .CLK(CLK), .S(S[1]));
  REGISTER1Bit register1bit_3 (.C(C[2]), .WE(WE), .CLK(CLK), .S(S[2]));
  REGISTER1Bit register1bit_4 (.C(C[3]), .WE(WE), .CLK(CLK), .S(S[3]));
  REGISTER1Bit register1bit_5 (.C(C[4]), .WE(WE), .CLK(CLK), .S(S[4]));
  REGISTER1Bit register1bit_6 (.C(C[5]), .WE(WE), .CLK(CLK), .S(S[5]));
  REGISTER1Bit register1bit_7 (.C(C[6]), .WE(WE), .CLK(CLK), .S(S[6]));
  REGISTER1Bit register1bit_8 (.C(C[7]), .WE(WE), .CLK(CLK), .S(S[7]));
endmodule

module REGISTER24Bits (
  input  [23:0] C,
  input  WE,
  input  CLK,
  output [23:0] S
);

  REGISTER8Bits register8bits_1 (.C(C[7:0]), .WE(WE), .CLK(CLK), .S(S[7:0]));
  REGISTER8Bits register8bits_2 (.C(C[15:8]), .WE(WE), .CLK(CLK), .S(S[15:8]));
  REGISTER8Bits register8bits_3 (.C(C[23:16]), .WE(WE), .CLK(CLK), .S(S[23:16]));
endmodule

module REGISTERFILE (
  input  [7:0] C,
  input  WE1,
  input  WE2,
  input  WE3,
  input  WE4,
  input  WE5,
  input  WE6,
  input  WE7,
  input  WE8,
  output [7:0] R1,
  output [7:0] R2,
  output [7:0] R3,
  output [7:0] R4,
  output [7:0] R5,
  output [7:0] R6,
  output [7:0] R7,
  output RCMP
);

  wire CLK_out;

  Clock CLK (.out(CLK_out));
  REGISTER8Bits register8bits_1 (.C(C), .WE(WE1), .CLK(CLK_out), .S(R1));
  REGISTER8Bits register8bits_2 (.C(C), .WE(WE2), .CLK(CLK_out), .S(R2));
  REGISTER8Bits register8bits_3 (.C(C), .WE(WE3), .CLK(CLK_out), .S(R3));
  REGISTER8Bits register8bits_4 (.C(C), .WE(WE4), .CLK(CLK_out), .S(R4));
  REGISTER8Bits register8bits_5 (.C(C), .WE(WE5), .CLK(CLK_out), .S(R5));
  REGISTER8Bits register8bits_6 (.C(C), .WE(WE6), .CLK(CLK_out), .S(R6));
  REGISTER8Bits register8bits_7 (.C(C), .WE(WE7), .CLK(CLK_out), .S(R7));
  REGISTER1Bit register1bit_1 (.C(C[0]), .WE(WE8), .CLK(CLK_out), .S(RCMP));
endmodule

module DECODE (
  input  [23:0] IFetched,
  input  WE,
  output RFWE,
  output [2:0] slctC,
  output [2:0] slctB,
  output [2:0] slctA,
  output [5:0] slctOP
);

  wire and_1_out, and_2_out, CLK_out, not_3_out, not_4_out, not_5_out;
  wire [2:0] register24bits_1_s_2;
  wire [23:3] register24bits_1_s;

  Clock CLK (.out(CLK_out));
  REGISTER24Bits register24bits_1 (
    .C(IFetched), .WE(WE), .CLK(CLK_out),
    .S({register24bits_1_s[23:19], slctOP[3], slctOP[1:0], register24bits_1_s[15], slctA, register24bits_1_s[11:3], register24bits_1_s_2}));
  or or_1 (RFWE, register24bits_1_s_2[0], register24bits_1_s_2[1], register24bits_1_s_2[2], register24bits_1_s[3], register24bits_1_s[4], register24bits_1_s[5], register24bits_1_s[6], register24bits_1_s[7], register24bits_1_s[8], register24bits_1_s[9], register24bits_1_s[10], register24bits_1_s[11], slctA[0], slctA[1], slctA[2], register24bits_1_s[15], slctOP[0], slctOP[1], slctOP[3], register24bits_1_s[19], register24bits_1_s[20], register24bits_1_s[21], register24bits_1_s[22], register24bits_1_s[23]);
  not not_1 (slctOP[4], register24bits_1_s[19]);
  not not_2 (slctOP[5], register24bits_1_s[20]);
  MUX1_3Bits mux1_3bits_1 (.S1(3'b000), .S2(register24bits_1_s[10:8]), .slct(not_3_out), .S(slctB));
  not not_3 (not_3_out, and_1_out);
  and and_1 (and_1_out, slctOP[5], not_4_out);
  not not_4 (not_4_out, slctOP[4]);
  MUX1_3Bits mux1_3bits_2 (.S1(3'b111), .S2(register24bits_1_s_2), .slct(not_5_out), .S(slctC));
  not not_5 (not_5_out, and_2_out);
  and and_2 (and_2_out, slctOP[4], slctOP[5]);

  assign slctOP[2] = slctOP[3];
endmodule

module FETCH (
  input  [23:0] IRAM,
  input  WE,
  output [23:0] IFetched
);

  wire CLK_out;

  Clock CLK (.out(CLK_out));
  REGISTER24Bits register24bits_1 (.C(IRAM), .WE(WE), .CLK(CLK_out), .S(IFetched));
endmodule

module INC (
  input  [7:0] A,
  output [7:0] S
);

  INC8Bits inc8bits_1 (.A(A), .S(S));  // open: O
endmodule

module PC (
  input  [7:0] C,
  input  WE,
  output [7:0] S
);

  wire CLK_out;

  Clock CLK (.out(CLK_out));
  REGISTER8Bits register8bits_1 (.C(C), .WE(WE), .CLK(CLK_out), .S(S));
endmodule

module AR8PROCESSOR (
);

  wire clock_1_out, dec3_1bit_1_we1, dec3_1bit_1_we2, dec3_1bit_1_we3, dec3_1bit_1_we4, dec3_1bit_1_we5,
       dec3_1bit_1_we6, dec3_1bit_1_we7, dec3_1bit_1_we8, decode_1_rfwe;
  wire [0:0] registerfile_1_rcmp;
  wire [2:0] decode_1_slcta, decode_1_slctb, decode_1_slctc;
  wire [5:0] decode_1_slctop;
  wire [7:0] alu_1_s, inc_1_s, mux3_8bits_1_s, mux3_8bits_2_s, pc_1_s, registerfile_1_r1, registerfile_1_r2,
       registerfile_1_r3, registerfile_1_r4, registerfile_1_r5, registerfile_1_r6, registerfile_1_r7;
  wire [23:0] fetch_1_ifetched, ram_1_dout;

  PC pc_1 (.C(inc_1_s), .WE(1'b1), .S(pc_1_s));
  Clock clock_1 (.out(clock_1_out));
  RAM #(.dataWidth(24)) ram_1 (.addr(pc_1_s), .we(1'b0), .oe(1'b1), .clk(clock_1_out), .dout(ram_1_dout));  // open: din
  INC inc_1 (.A(pc_1_s), .S(inc_1_s));
  FETCH fetch_1 (.IRAM(ram_1_dout), .WE(1'b1), .IFetched(fetch_1_ifetched));
  DEC3_1Bit dec3_1bit_1 (
    .WE(decode_1_rfwe), .slct(decode_1_slctc), .WE1(dec3_1bit_1_we1), .WE2(dec3_1bit_1_we2),
    .WE3(dec3_1bit_1_we3), .WE4(dec3_1bit_1_we4), .WE5(dec3_1bit_1_we5), .WE6(dec3_1bit_1_we6),
    .WE7(dec3_1bit_1_we7), .WE8(dec3_1bit_1_we8));
  DECODE decode_1 (
    .IFetched(fetch_1_ifetched), .WE(1'b1), .slctOP(decode_1_slctop), .slctC(decode_1_slctc),
    .RFWE(decode_1_rfwe), .slctA(decode_1_slcta), .slctB(decode_1_slctb));
  REGISTERFILE registerfile_1 (
    .WE1(dec3_1bit_1_we1), .WE2(dec3_1bit_1_we2), .WE3(dec3_1bit_1_we3), .WE4(dec3_1bit_1_we4),
    .WE5(dec3_1bit_1_we5), .WE6(dec3_1bit_1_we6), .WE7(dec3_1bit_1_we7), .WE8(dec3_1bit_1_we8), .C(alu_1_s),
    .R1(registerfile_1_r1), .R2(registerfile_1_r2), .R3(registerfile_1_r3), .R4(registerfile_1_r4),
    .R5(registerfile_1_r5), .R6(registerfile_1_r6), .R7(registerfile_1_r7), .RCMP(registerfile_1_rcmp[0]));
  MUX3_8Bits mux3_8bits_1 (
    .S8({{7{1'b0}}, registerfile_1_rcmp[0]}), .S1(registerfile_1_r1), .S2(registerfile_1_r2),
    .S3(registerfile_1_r3), .S4(registerfile_1_r4), .S5(registerfile_1_r5), .S6(registerfile_1_r6),
    .S7(registerfile_1_r7), .slct(decode_1_slctb), .S(mux3_8bits_1_s));
  MUX3_8Bits mux3_8bits_2 (
    .S8({{7{1'b0}}, registerfile_1_rcmp[0]}), .S1(registerfile_1_r1), .S2(registerfile_1_r2),
    .S3(registerfile_1_r3), .S4(registerfile_1_r4), .S5(registerfile_1_r5), .S6(registerfile_1_r6),
    .S7(registerfile_1_r7), .slct(decode_1_slcta), .S(mux3_8bits_2_s));
  ALU alu_1 (.A(mux3_8bits_2_s), .OP(decode_1_slctop), .B(mux3_8bits_1_s), .S(alu_1_s));  // open: E
endmodule
